# Fritzing sketch skps (saved by Fritzing 0.9.3b)
breadboards: 1

parts:
  Mod1 = Raspberry Pi 4B
  R1 = Resistor [tolerance=±5% resistance=4.7k package=THT]
  Part1 = Adafruit VL530X Time of Flight Distance Sensor [part_number="Adafruit #3317"]
  Part2 = Logic Level Converter
  J1 = Basic Servo
  R4 = Resistor [tolerance=±5% resistance=4.7k package=THT]  # not connected
  R5 = Resistor [tolerance=±5% resistance=4.7k package=THT]  # not connected
  R6 = Resistor [tolerance=±5% resistance=4.7k package=THT]  # not connected
  R7 = Resistor [tolerance=±5% resistance=4.7k package=THT]
  R8 = Resistor [tolerance=±5% resistance=4.7k package=THT]

nets:
  3V3: Mod1.3V3, R1.Pin_1, Part1.VCC, Part2.LV, R7.Pin_1, R8.Pin_1
  5V: Mod1.5V, Part2.HV, J1.vcc
  N1: Mod1.GPIO2, Part1.SDA, R8.Pin_0
  N2: Mod1.GPIO3, Part1.SCL, R7.Pin_0
  GND: Mod1.GND, Part1.GND, Part2.GND, J1.gnd
  N3: Mod1.GPIO4, Part2.TX2_LV
  N4: R1.Pin_0, Part1.XSHUT
  N5: Part2.TX2_HV, J1.pulse

custom parts:
  Adafruit VL530X Time of Flight Distance Sensor: The VL53L0X is a Time of Flight distance sensor like no other you've used! The sensor contains a very tiny invisible laser source, and a matching sensor. The VL53L0X can detect the "time of flight", or how long the light has taken to bounce back to the sensor. Since it uses a very narrow light source, it is good for determining distance of only the surface directly in front of it. Unlike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
